# Fritzing sketch circuit diagram (saved by Fritzing 0.9.3b)

parts:
  Part1 = Arduino Uno (Rev3) - ICSP
  J1 = Basic Servo
  J2 = Basic Servo
  J3 = Basic Servo
  J4 = Basic Servo
  J5 = Basic Servo
  J6 = Basic Servo
  J7 = Power Jack [package=power_jack_combo]  # not connected
  Part2 = Bluetooth HC-05 Macho

nets:
  N1: Part1.D8, J4.pulse
  N2: Part1.D9_PWM, J5.pulse
  N3: Part1.D10_PWM/SS, J6.pulse
  N4: Part1.D3_PWM, Part2.RXD
  N5: Part1.D4, Part2.TXD
  N6: Part1.D5_PWM, J1.pulse
  N7: Part1.D6_PWM, J2.pulse
  N8: Part1.D7, J3.pulse
  VCC: Part1.5V, J2.vcc, J3.vcc, J4.vcc, J5.vcc, J6.vcc

notes:
  5V DC Input
  Waist
  Shoulder
  Elbow
  Jaw Roll
  Jaw Pitch
  Gripper
  Nikhil Sharma
